# Fritzing sketch Termostatoa (saved by Fritzing 0.9.3b)

parts:
  U1 = NodeMCU V1.0
  DHT1 = Humidity and Temperature Sensor DHT11
  Part1 = KY-019 5V Relay Module [package="Breakout board"]

nets:
  N1: U1.D2, Part1.+
  N2: U1.D4, DHT1.Data-signal
  3V3: U1.3V3, DHT1.Vcc
  N3: U1.GND, DHT1.GND_2, Part1.-
  N4: U1.Vin, Part1.S

notes:
  Termostatoa V.1

custom parts:
  NodeMCU V1.0: ESP8266 based NodeMCU
  Humidity and Temperature Sensor DHT11: Digital relative humidity & temperature sensor DHT11
  KY-019 5V Relay Module: KY-019 5V Relay module, used to control AC circuits.
